// Logisim project X.circ as structural Verilog: 7 circuits, main circuit main
module main (
  input  Sign_A,
  input  Sign_B,
  input  A0,
  input  A1,
  input  B0,
  input  B1,
  input  [1:0] in_7,
  input  [1:0] in_8,
  input  [1:0] in_9,
  input  [1:0] in_10,
  input  [1:0] in_11,
  input  [1:0] in_12,
  input  [1:0] in_13,
  output C0,
  output Sign,
  output C1,
  output S2,
  output C2,
  output S1,
  output S0,
  output C3,
  output Sign_2,
  output Divided_by_zero,
  output minus_ve_falg,
  output zero_flag,
  output C0_2,
  output C1_2
);

  wire multiplexer_1_out, multiplexer_2_out, multiplexer_3_out, multiplexer_4_out, multiplexer_5_out,
       multiplexer_6_out, multiplexer_7_out, n7_segment_display_driver_1_p5, n7_segment_display_driver_1_p6,
       n7_segment_display_driver_1_p7, n7_segment_display_driver_1_p8, n7_segment_display_driver_1_p9,
       n7_segment_display_driver_1_p10, n7_segment_display_driver_1_p11, zero_flag_3_input_1_out_4,
       zero_flag_4_input_1_out_5;

  multi multiplex (
    .SignB(Sign_B), .SignA(Sign_A), .A0(A0), .A1(A1), .B0(B0), .B1(B1), .C0(C0), .C1(C1), .C2(C2), .C3(C3),
    .Sign(Sign_2));
  zero_flag_4_input zero_flag_4_input_1 (.in_1(C3), .in_2(C2), .in_3(C1), .in_4(C0), .out_5(zero_flag_4_input_1_out_5));
  zero_flag_3_input zero_flag_3_input_1 (.in_1(S2), .in_2(S1), .in_3(S0), .out_4(zero_flag_3_input_1_out_4));
  remainder remainder_1 (
    .SignA(Sign_A), .A1(A1), .A0(A0), .SignB(Sign_B), .B1(B1), .B0(B0), .Divided_by_zero(Divided_by_zero),
    .minus_ve_flag(minus_ve_falg), .Zero_flag(zero_flag), .C0(C0_2), .C1(C1_2));
  adder_and_substructor adder_and_substructor_1 (
    .SA(Sign_A), .SB___Subtraction(Sign_B), .A1(A1), .A0(A0), .B1(B1), .B0(B0), .Sign(Sign), .S2(S2),
    .S1(S1), .S0(S0));
  Multiplexer #(.select(2)) multiplexer_1 (
    .in0(S2), .in1(C2), .in2(1'b0), .in3(1'b0), .out(multiplexer_1_out), .sel(in_7));  // open: en
  Multiplexer #(.select(2)) multiplexer_2 (
    .in0(S1), .in1(C1), .in2(C1_2), .in3(1'b0), .out(multiplexer_2_out), .sel(in_8));  // open: en
  Multiplexer #(.select(2)) multiplexer_3 (
    .in0(S0), .in1(C0), .in2(C0_2), .in3(1'b0), .out(multiplexer_3_out), .sel(in_9));  // open: en
  Multiplexer #(.select(2)) multiplexer_4 (
    .in0(1'b0), .in1(C3), .in2(1'b0), .in3(1'b0), .out(multiplexer_4_out), .sel(in_10));  // open: en
  Multiplexer #(.select(2)) multiplexer_5 (
    .in0(Sign), .in1(Sign_2), .in2(minus_ve_falg), .in3(1'b0), .out(multiplexer_5_out), .sel(in_11));  // open: en
  Multiplexer #(.select(2)) multiplexer_6 (
    .in0(1'b0), .in1(1'b0), .in2(Divided_by_zero), .in3(1'b0), .out(multiplexer_6_out), .sel(in_12));  // open: en
  Multiplexer #(.select(2)) multiplexer_7 (
    .in0(zero_flag_3_input_1_out_4), .in1(zero_flag_4_input_1_out_5), .in2(zero_flag), .in3(1'b0),
    .out(multiplexer_7_out), .sel(in_13));  // open: en
  // Simple_buzzer simple_buzzer_1: pin names not known; wires that end beside it: multiplexer_6_out
  LED u_divided_by_zero (.in(multiplexer_6_out));
  LED u_zero_flag (.in(multiplexer_7_out));
  // _7_segment_display_driver 7_segment_display_driver_1: pin names not known; wires that end beside it: multiplexer_4_out, multiplexer_1_out, multiplexer_2_out, multiplexer_3_out, n7_segment_display_driver_1_p5, n7_segment_display_driver_1_p6, n7_segment_display_driver_1_p7, n7_segment_display_driver_1_p8, n7_segment_display_driver_1_p9, n7_segment_display_driver_1_p10, n7_segment_display_driver_1_p11
  _7_Segment_Display u_7_segment_display_1 (.g(multiplexer_5_out));  // open: f, a, b, e, d, c, dp
  _7_Segment_Display u_7_segment_display_2 (
    .g(n7_segment_display_driver_1_p11), .f(n7_segment_display_driver_1_p10),
    .a(n7_segment_display_driver_1_p5), .b(n7_segment_display_driver_1_p6),
    .e(n7_segment_display_driver_1_p9), .d(n7_segment_display_driver_1_p8), .c(n7_segment_display_driver_1_p7));  // open: dp

  // Notes on the sheet:
  //   addition or substraction ->00
  //   multiplication -> 01
  //   remainder -> 10
endmodule

module FA (
  input  carry,
  input  A,
  input  B,
  output S,
  output C
);

  wire and_1_out, and_2_out, xor_1_out;

  xor xor_1 (xor_1_out, A, B);
  and and_1 (and_1_out, A, B);
  xor xor_2 (S, carry, xor_1_out);
  and and_2 (and_2_out, carry, xor_1_out);
  or or_1 (C, and_2_out, and_1_out);
endmodule

module adder_and_substructor (
  input  A1,
  input  A0,
  input  B1,
  input  B0,
  input  SA,
  input  SB___Subtraction,
  output Sign,
  output S2,
  output S1,
  output S0
);

  wire and_1_out, and_2_out, and_3_out, and_4_out, and_5_out, and_6_out, fa_2_c, fa_2_s, fa_3_c, fa_3_s,
       fa_4_c, fa_4_s, n7_segment_display_driver_1_p5, n7_segment_display_driver_1_p6,
       n7_segment_display_driver_1_p7, n7_segment_display_driver_1_p8, n7_segment_display_driver_1_p9,
       n7_segment_display_driver_1_p10, n7_segment_display_driver_1_p11, xor_1_out, xor_2_out, xor_3_out,
       xor_5_out, xor_6_out, xor_7_out, xor_8_out, xor_10_out, xor_11_out, xor_12_out, xor_13_out,
       xor_15_out, xor_16_out, xor_17_out, xor_18_out;

  FA fa_1 (.carry(fa_2_c), .A(SB___Subtraction), .B(SA), .S(Sign));  // open: C
  xor xor_1 (xor_1_out, 1'b0, SA);
  xor xor_2 (xor_2_out, xor_1_out, and_1_out);
  FA fa_2 (.carry(xor_2_out), .A(xor_12_out), .B(fa_3_c), .S(fa_2_s), .C(fa_2_c));
  and and_1 (and_1_out, xor_5_out, and_3_out);
  xor xor_3 (xor_3_out, Sign, fa_2_s);
  xor xor_4 (S2, xor_3_out, and_2_out);
  xor xor_5 (xor_5_out, A1, SA);
  xor xor_6 (xor_6_out, xor_5_out, and_3_out);
  FA fa_3 (.carry(xor_6_out), .A(xor_16_out), .B(fa_4_c), .S(fa_3_s), .C(fa_3_c));
  and and_2 (and_2_out, xor_7_out, and_4_out);
  and and_3 (and_3_out, xor_8_out, SA);
  xor xor_7 (xor_7_out, fa_3_s, Sign);
  xor xor_8 (xor_8_out, A0, SA);
  FA fa_4 (.carry(1'b0), .A(xor_18_out), .B(xor_10_out), .S(fa_4_s), .C(fa_4_c));
  and and_4 (and_4_out, xor_13_out, Sign);
  xor xor_9 (S1, xor_7_out, and_4_out);
  xor xor_10 (xor_10_out, xor_8_out, SA);
  xor xor_11 (xor_11_out, 1'b0, SB___Subtraction);
  xor xor_12 (xor_12_out, xor_11_out, and_5_out);
  xor xor_13 (xor_13_out, Sign, fa_4_s);
  xor xor_14 (S0, xor_13_out, Sign);
  and and_5 (and_5_out, xor_15_out, and_6_out);
  xor xor_15 (xor_15_out, B1, SB___Subtraction);
  xor xor_16 (xor_16_out, xor_15_out, and_6_out);
  and and_6 (and_6_out, xor_17_out, SB___Subtraction);
  xor xor_17 (xor_17_out, B0, SB___Subtraction);
  xor xor_18 (xor_18_out, xor_17_out, SB___Subtraction);
  // _7_segment_display_driver 7_segment_display_driver_1: pin names not known; wires that end beside it: 1'b0, S2, S1, S0, n7_segment_display_driver_1_p5, n7_segment_display_driver_1_p6, n7_segment_display_driver_1_p7, n7_segment_display_driver_1_p8, n7_segment_display_driver_1_p9, n7_segment_display_driver_1_p10, n7_segment_display_driver_1_p11
  _7_Segment_Display u_7_segment_display_1 (.g(Sign));  // open: f, a, b, e, d, c, dp
  _7_Segment_Display u_7_segment_display_2 (
    .g(n7_segment_display_driver_1_p11), .f(n7_segment_display_driver_1_p10),
    .a(n7_segment_display_driver_1_p5), .b(n7_segment_display_driver_1_p6),
    .e(n7_segment_display_driver_1_p9), .d(n7_segment_display_driver_1_p8), .c(n7_segment_display_driver_1_p7));  // open: dp
endmodule

module multi (
  input  SignB,
  input  SignA,
  input  A0,
  input  A1,
  input  B0,
  input  B1,
  output C0,
  output C1,
  output C2,
  output C3,
  output Sign
);

  wire A0B1_out, A1B0_out, A1B1_out, and_1_out, n7_segment_display_driver_1_p5,
       n7_segment_display_driver_1_p6, n7_segment_display_driver_1_p7, n7_segment_display_driver_1_p8,
       n7_segment_display_driver_1_p9, n7_segment_display_driver_1_p10, n7_segment_display_driver_1_p11;

  xor xor_1 (Sign, SignB, SignA);
  and A0B0 (C0, A0, B0);
  and A1B0 (A1B0_out, A1, B0);
  and A0B1 (A0B1_out, A0, B1);
  and A1B1 (A1B1_out, A1, B1);
  xor xor_2 (C1, A1B0_out, A0B1_out);
  and and_1 (and_1_out, A0B1_out, A1B0_out);
  xor xor_3 (C2, and_1_out, A1B1_out);
  and and_2 (C3, and_1_out, A1B1_out);
  // _7_segment_display_driver 7_segment_display_driver_1: pin names not known; wires that end beside it: C3, C2, C1, C0, n7_segment_display_driver_1_p5, n7_segment_display_driver_1_p6, n7_segment_display_driver_1_p7, n7_segment_display_driver_1_p8, n7_segment_display_driver_1_p9, n7_segment_display_driver_1_p10, n7_segment_display_driver_1_p11
  _7_Segment_Display u_7_segment_display_1 (.g(Sign));  // open: f, a, b, e, d, c, dp
  _7_Segment_Display u_7_segment_display_2 (
    .g(n7_segment_display_driver_1_p11), .f(n7_segment_display_driver_1_p10),
    .a(n7_segment_display_driver_1_p5), .b(n7_segment_display_driver_1_p6),
    .e(n7_segment_display_driver_1_p9), .d(n7_segment_display_driver_1_p8), .c(n7_segment_display_driver_1_p7));  // open: dp
endmodule

module remainder (
  input  SignA,
  input  A1,
  input  A0,
  input  SignB,
  input  B1,
  input  B0,
  output Divided_by_zero,
  output Zero_flag,
  output C0,
  output minus_ve_flag,
  output C1
);

  wire nand_1_out, nor_1_out, not_1_out, or_1_out, or_2_out, or_3_out;

  or or_1 (or_1_out, B0, B1);
  or or_2 (or_2_out, B1, B0);
  nand nand_1 (nand_1_out, A1, B0);
  not not_1 (not_1_out, A0);
  and and_1 (C0, A0, B1, nand_1_out);
  and and_2 (C1, A1, not_1_out, B1, B0);
  not not_2 (Divided_by_zero, or_1_out);
  nor nor_1 (nor_1_out, C1, C0);
  or or_3 (or_3_out, C0, C1);
  and and_3 (Zero_flag, or_2_out, nor_1_out);
  and and_4 (minus_ve_flag, or_3_out, SignA);
endmodule

module zero_flag_4_input (
  input  in_1,
  input  in_2,
  input  in_3,
  input  in_4,
  output out_5
);

  nor nor_1 (out_5, in_1, in_2, in_3, in_4);
endmodule

module zero_flag_3_input (
  input  in_1,
  input  in_2,
  input  in_3,
  output out_4
);

  nor nor_1 (out_4, in_1, in_2, in_3);
endmodule
